// Logisim project computer.circ as structural Verilog: 12 circuits, main circuit main
module main (
  input  A_OUT,
  input  A_IN,
  input  B_OUT,
  input  B_IN,
  input  RAM_OUT,
  input  RAM_IN,
  input  PAGE_IN,
  input  ADDR_IN,
  input  MAR____ADRB,
  input  Data,
  input  ADRB____MAR,
  input  SUBTRACT,
  input  SUM____ACC,
  input  in_14,
  input  LATCH_ACC,
  input  FLAG_IN,
  input  ACC_OUT,
  input  ACC_IN,
  input  JUMP,
  input  COUNT,
  input  PC_OUT,
  input  HALT,
  input  CIR_OP_IN,
  input  CIR_ARG_OUT,
  input  CIR_ARG_IN,
  input  OUTPUT
);

  wire alu_1_c, alu_1_z, CLK, flag_1_c_out, flag_1_z_out;
  wire [2:0] \µ_code_step_1_step ;
  wire [3:0] output_1_high, output_1_low;
  wire [7:0] alu_1_d_out, cir_1_op;
  wire [15:0] mar_1_a_out;
  wire [31:24] decoder_1_c_2;

  clock clock_1 (.HALT(HALT), .CLK(CLK));
  // Probe on mar_1_a_out
  // Probe on alu_1_d_out
  mar mar_1 (
    .CLK(CLK), .A_IN(mar_1_a_out), .D(alu_1_d_out), .A_OUT(mar_1_a_out), .ADDR_IN(ADDR_IN),
    .FROM_ADRB(ADRB____MAR), .TO_ADRB(MAR____ADRB), .PAGE_IN(PAGE_IN));
  alu alu_1 (
    .D_IN(alu_1_d_out), .LATCH_ACC(LATCH_ACC), .SUB(SUBTRACT), .SUM__ACC(SUM____ACC), .Z(alu_1_z),
    .ACC_IN(ACC_IN), .ACC_OUT(ACC_OUT), .D_OUT(alu_1_d_out), .CLK(CLK), .C(alu_1_c));
  assign mar_1_a_out = Data ? 16'hf0f0 : 16'bz;  // Controlled_Buffer controlled_buffer_1
  assign alu_1_d_out = in_14 ? 8'h7 : 8'bz;  // Controlled_Buffer controlled_buffer_2
  flag flag_1 (.Z_IN(alu_1_z), .C_IN(alu_1_c), .LOAD(FLAG_IN), .Z_OUT(flag_1_z_out), .C_OUT(flag_1_c_out), .CLK(CLK));
  Hex_Digit_Display hex_digit_display_1 (.value(mar_1_a_out[11:8]));  // open: dp
  Hex_Digit_Display hex_digit_display_2 (.value(mar_1_a_out[15:12]));  // open: dp
  Hex_Digit_Display hex_digit_display_3 (.value(alu_1_d_out[7:4]));  // open: dp
  Hex_Digit_Display hex_digit_display_4 (.value(alu_1_d_out[3:0]));  // open: dp
  register A (.D_IN(alu_1_d_out), .CLK(CLK), .D_OUT(alu_1_d_out), .IN(A_IN), .OUT(A_OUT));
  register B (.D_IN(alu_1_d_out), .CLK(CLK), .D_OUT(alu_1_d_out), .IN(B_IN), .OUT(B_OUT));
  ram ram_1 (.A(mar_1_a_out), .D_IN(alu_1_d_out), .D_OUT(alu_1_d_out), .OUT(RAM_OUT), .CLK(CLK), .IN(RAM_IN));
  pc pc_1 (.JUMP(JUMP), .A_IN(mar_1_a_out), .COUNT(COUNT), .A_OUT(mar_1_a_out), .CLK(CLK), .OUT(PC_OUT));
  cir cir_1 (
    .OP_IN(CIR_OP_IN), .D_IN(alu_1_d_out), .D_OUT(alu_1_d_out), .OP(cir_1_op), .CLK(CLK),
    .ARG_OUT(CIR_ARG_OUT), .ARG_IN(CIR_ARG_IN));
  \µ_code_step  \u_µ_code_step_1  (.CLK(CLK), .STEP(\µ_code_step_1_step ));
  Hex_Digit_Display hex_digit_display_5 (.value(mar_1_a_out[7:4]));  // open: dp
  Hex_Digit_Display hex_digit_display_6 (.value(mar_1_a_out[3:0]));  // open: dp
  decoder decoder_1 (
    .STEP(\µ_code_step_1_step ), .C(flag_1_c_out), .Z(flag_1_z_out), .OP(cir_1_op),
    .C_2({decoder_1_c_2, OUTPUT, CIR_ARG_IN, CIR_ARG_OUT, CIR_OP_IN, HALT, PC_OUT, COUNT, JUMP, ACC_IN, ACC_OUT, FLAG_IN, LATCH_ACC, SUM____ACC, SUBTRACT, ADRB____MAR, MAR____ADRB, ADDR_IN, PAGE_IN, RAM_IN, RAM_OUT, B_IN, B_OUT, A_IN, A_OUT}));
  Hex_Digit_Display hex_digit_display_7 (.value(output_1_high));  // open: dp
  Hex_Digit_Display hex_digit_display_8 (.value(output_1_low));  // open: dp
  \output  output_1 (.D(alu_1_d_out), .IN(OUTPUT), .CLK(CLK), .LOW(output_1_low), .HIGH(output_1_high));

  // Other names for the same wires on the sheet: C0 = A_OUT; C1 = A_IN; C2 = B_OUT; C3 = B_IN; C4 = RAM_OUT;
  //   C5 = RAM_IN; C6 = PAGE_IN; C7 = ADDR_IN; C8 = MAR____ADRB; C9 = ADRB____MAR; C10 = SUBTRACT; C11 = SUM____ACC;
  //   C12 = LATCH_ACC; C13 = FLAG_IN; C14 = ACC_OUT; C15 = ACC_IN; C16 = JUMP; C17 = COUNT; C18 = PC_OUT; C19 = HALT;
  //   C20 = CIR_OP_IN; C21 = CIR_ARG_OUT; C22 = CIR_ARG_IN; C23 = OUTPUT

  // Notes on the sheet:
  //   Manual Controls
  //   Clock
  //   Address
  //   Memory Address Register
  //   Arithmetic + Logic Unit
  //   Address Bus
  //   Microcode Stepper
  //   Data Bus
  //   A Register
  //   B Register
  //   Memory
  //   Program Counter
  //   Current Instruction
  //   Register
  //   Instruction Decoder
endmodule

// REG
module register (
  input  [7:0] D_IN,
  input  IN,
  input  OUT,
  input  CLK,
  output [7:0] D_OUT
);

  wire not_1_out;
  wire [7:0] register_1_q;

  not not_1 (not_1_out, CLK);
  Register register_1 (.D(D_IN), .en(IN), .Q(register_1_q), .clk(not_1_out));  // open: clr
  assign D_OUT = OUT ? register_1_q : 8'bz;  // Controlled_Buffer controlled_buffer_1
endmodule

// RAM
module ram (
  input  [7:0] D_IN,
  input  [15:0] A,
  input  OUT,
  input  CLK,
  input  IN,
  output [7:0] D_OUT
);

  wire and_1_out;
  wire [7:0] ram_1_data;

  and and_1 (and_1_out, ~CLK, IN);  // AND_Gate
  RAM #(.addrWidth(16)) ram_1 (.addr(A), .data(ram_1_data), .clk(and_1_out), .ld(OUT));  // open: sel, clr
  assign ram_1_data = IN ? D_IN : 8'bz;  // Controlled_Buffer controlled_buffer_1
  assign D_OUT = OUT ? ram_1_data : 8'bz;  // Controlled_Buffer controlled_buffer_2
endmodule

// MAR
module mar (
  input  CLK,
  input  [15:0] A_IN,
  input  [7:0] D,
  input  ADDR_IN,
  input  PAGE_IN,
  input  FROM_ADRB,
  input  TO_ADRB,
  output [15:0] A_OUT
);

  wire or_1_out, or_2_out;
  wire [7:0] multiplexer_1_out, multiplexer_2_out;

  Multiplexer #(.width(8), .enable("false")) multiplexer_1 (
    .in0(A_IN[7:0]), .in1(D), .out(multiplexer_1_out), .sel(ADDR_IN));
  register ADDR (.D_IN(multiplexer_1_out), .CLK(CLK), .D_OUT(A_OUT[7:0]), .IN(or_1_out), .OUT(TO_ADRB));
  or or_1 (or_1_out, ADDR_IN, FROM_ADRB);
  register PAGE (.D_IN(multiplexer_2_out), .CLK(CLK), .D_OUT(A_OUT[15:8]), .IN(or_2_out), .OUT(TO_ADRB));
  Multiplexer #(.width(8), .enable("false")) multiplexer_2 (
    .in0(A_IN[15:8]), .in1(D), .out(multiplexer_2_out), .sel(PAGE_IN));
  or or_2 (or_2_out, PAGE_IN, FROM_ADRB);
endmodule

// ALU
module alu (
  input  [7:0] D_IN,
  input  LATCH_ACC,
  input  SUB,
  input  CLK,
  input  SUM__ACC,
  input  ACC_IN,
  input  ACC_OUT,
  output C,
  output Z,
  output [7:0] D_OUT
);

  wire nor_1_out, nor_2_out, nor_3_out, nor_4_out, not_1_out, not_2_out, or_1_out;
  wire [7:0] Accumulator_q, adder_1_out, bit_extender_1_out, controlled_buffer_1_out,
       controlled_buffer_2_out, Latch_q, multiplexer_1_out, xor_1_out;

  Multiplexer #(.width(8), .enable("false")) multiplexer_1 (
    .in0(D_IN), .in1(controlled_buffer_1_out), .out(multiplexer_1_out), .sel(SUM__ACC));
  assign controlled_buffer_1_out = SUM__ACC ? adder_1_out : 8'bz;  // Controlled_Buffer controlled_buffer_1
  or or_1 (or_1_out, SUM__ACC, ACC_IN);
  Register Accumulator (.D(multiplexer_1_out), .en(or_1_out), .Q(Accumulator_q), .clk(not_1_out));  // open: clr
  not not_1 (not_1_out, CLK);
  assign controlled_buffer_2_out = LATCH_ACC ? Accumulator_q : 8'bz;  // Controlled_Buffer controlled_buffer_2
  not not_2 (not_2_out, CLK);
  assign D_OUT = ACC_OUT ? Accumulator_q : 8'bz;  // Controlled_Buffer controlled_buffer_3
  Register Latch (.D(controlled_buffer_2_out), .en(LATCH_ACC), .Q(Latch_q), .clk(not_2_out));  // open: clr
  and and_1 (Z, nor_1_out, nor_2_out, nor_3_out, nor_4_out);
  assign bit_extender_1_out = {{7{SUB}}, SUB};  // Bit_Extender bit_extender_1
  nor nor_1 (nor_1_out, adder_1_out[0], adder_1_out[1]);
  nor nor_2 (nor_2_out, adder_1_out[2], adder_1_out[3]);
  nor nor_3 (nor_3_out, adder_1_out[4], adder_1_out[5]);
  nor nor_4 (nor_4_out, adder_1_out[6], adder_1_out[7]);
  assign xor_1_out = bit_extender_1_out ^ D_IN;  // XOR_Gate xor_1, 8 bits wide
  Adder adder_1 (.a(Latch_q), .b(xor_1_out), .out(adder_1_out), .cin(SUB), .cout(C));
  // Probe on adder_1_out
endmodule

// FLAG
module flag (
  input  Z_IN,
  input  C_IN,
  input  LOAD,
  input  CLK,
  output Z_OUT,
  output C_OUT
);

  wire not_1_out;

  Register #(.width(2)) register_1 (.D({C_IN, Z_IN}), .en(LOAD), .Q({C_OUT, Z_OUT}), .clk(not_1_out));  // open: clr
  not not_1 (not_1_out, CLK);
endmodule

// CLOCK
module clock (
  input  HALT,
  output CLK
);

  wire clock_1_out, not_1_out;

  Clock clock_1 (.out(clock_1_out));
  and and_1 (CLK, clock_1_out, not_1_out);
  not not_1 (not_1_out, HALT);
endmodule

// PC
module pc (
  input  JUMP,
  input  [15:0] A_IN,
  input  OUT,
  input  COUNT,
  input  CLK,
  output [15:0] A_OUT
);

  wire xor_1_out;
  wire [15:0] counter_1_q;

  Counter #(.width(16), .max('hffff)) counter_1 (
    .load(JUMP), .D(A_IN), .count(COUNT), .Q(counter_1_q), .clk(xor_1_out));  // open: carry, clr
  xor xor_1 (xor_1_out, COUNT, ~CLK);  // XOR_Gate
  assign A_OUT = OUT ? counter_1_q : 16'bz;  // Controlled_Buffer controlled_buffer_1
endmodule

// CIR
module cir (
  input  OP_IN,
  input  [7:0] D_IN,
  input  CLK,
  input  ARG_OUT,
  input  ARG_IN,
  output [7:0] OP,
  output [7:0] D_OUT
);

  Register register_1 (.D(D_IN), .en(OP_IN), .Q(OP), .clk(CLK));  // open: clr
  register ARG (.D_IN(D_IN), .CLK(CLK), .D_OUT(D_OUT), .IN(ARG_IN), .OUT(ARG_OUT));
endmodule

// DEC
module decoder (
  input  [2:0] STEP,
  input  C,
  input  Z,
  input  [7:0] OP,
  output [31:0] C_2
);

  ROM #(.addrWidth(13), .dataWidth(32)) rom_1 (.addr({OP, Z, C, STEP}), .data(C_2));  // open: sel
endmodule

// STP
module \µ_code_step  (
  input  CLK,
  output [2:0] STEP
);

  Counter #(.width(3), .max('h7)) counter_1 (.count(1'b1), .Q(STEP), .clk(CLK));  // open: load, D, carry, clr
endmodule

// OUT
module \output  (
  input  [7:0] D,
  input  IN,
  input  CLK,
  output [3:0] LOW,
  output [3:0] HIGH
);

  wire not_1_out;

  Register register_1 (.D(D), .en(IN), .Q({HIGH, LOW}), .clk(not_1_out));  // open: clr
  not not_1 (not_1_out, CLK);
endmodule
